# Fritzing sketch WaiterBotRobotConnections (saved by Fritzing 0.9.4)

parts:
  U2 = ESP 32 DEVKIT DOIT
  L298N1 = L298N DC motor driver
  Part1 = SRF05 Ultrasonic Rangefinder
  Part2 = SRF05 Ultrasonic Rangefinder
  Keyes1 = Keyes IR Infrared Sensor Switch Module
  Keyes2 = Keyes IR Infrared Sensor Switch Module
  Keyes3 = Keyes IR Infrared Sensor Switch Module
  Keyes4 = Keyes IR Infrared Sensor Switch Module
  Keyes5 = Keyes IR Infrared Sensor Switch Module
  Keyes6 = Keyes IR Infrared Sensor Switch Module
  Keyes7 = Keyes IR Infrared Sensor Switch Module
  Part3 = HX711 Weighing Sensor Module
  M1 = DC Motor
  M2 = DC Motor
  BAT1 = Battery Holders [package=battery-aa]
  VCC1 = 4 x AAA Battery Mount
  Load_Cell1 = Load Cell - Red/white/black/green

nets:
  N1: U2.D23, Keyes5.out
  N2: U2.D22, U2.D18, U2.D5, U2.TX2, U2.RX2, L298N1.ENA, L298N1.ENB, L298N1.IN2, L298N1.IN3, L298N1.IN4
  N3: U2.TX0, L298N1.IN1
  N4: U2.D21, Keyes6.out
  N5: U2.D19, Keyes7.out
  N6: U2.D26, Part3.CK/TX
  N7: U2.D25, Part3.DO/RX
  N8: U2.D33, Part1.Trig, Part1.Echo
  N9: U2.D32, Part2.Trig, Part2.Echo
  N10: U2.D35, Keyes1.out
  N11: U2.D34, Keyes2.out
  N12: U2.VN, Keyes3.out
  N13: U2.VP, Keyes4.out
  N14: L298N1.OUT1, M1.pin_2
  N15: L298N1.OUT2, M1.pin_1
  N16: L298N1.OUT3, M2.pin_2
  N17: L298N1.OUT4, M2.pin_1
  N18: L298N1.12V, VCC1.+
  N19: L298N1.GND, VCC1.-
  VCC: Part1.VCC, Part2.VCC
  N20: Part1.GND, BAT1.-
  N21: Keyes6.VCC, BAT1.+
  N22: Part3.E+, Load_Cell1.wire1
  N23: Part3.E-, Load_Cell1.wire3
  N24: Part3.A+, Load_Cell1.wire2
  N25: Part3.A-, Load_Cell1.wire4

custom parts:
  L298N DC motor driver: 2x DC motor driver with 78M05 positive voltage regulator (7..35 V) L298N: max 46 V, 2 A Set 5 V Enable jumper to enable 5 V regultor (needed for the L298N) and +5 V output at screw terminal or supply external +5 V at screw terminal Set ENA and/or ENB to +5 V to enable motor permanently or supply ENA and/or ENB with PWM signal IN1 and IN2 set rotation directory for motor A (OUT1/OUT2) IN2 and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
  Keyes IR Infrared Sensor Switch Module: An infrared obstacle detector
  Load Cell - Red/white/black/green: A rectangle load cell/weighting pressure Sensor with four wires - Red, white, black, green. Normally corresponding with E+, E-, A+, A- respectively.
